// Digital circuit Address Register.dig as structural Verilog
module Address_Register (
  input  [5:0] Control,
  input  [15:0] XFER,
  input  Clock,
  output [15:0] ADDR,
  output [15:0] I
);

  wire delay_1_out, delay_2_out, or_1_out;
  wire [15:0] register_1_q, register_2_q;

  assign XFER = Control[5] ? register_1_q : 16'bz;  // Driver driver_1
  assign ADDR = Control[4] ? register_2_q : 16'bz;  // Driver driver_2
  Register #(.Bits(16)) register_1 (.D(I), .C(Clock), .en(1'b1), .Q(register_1_q));
  Register #(.Bits(16)) register_2 (.D(I), .C(Clock), .en(1'b1), .Q(register_2_q));
  or or_1 (or_1_out, Control[2], Control[1]);
  Delay delay_1 (.in(Clock), .out(delay_1_out));
  Delay delay_2 (.in(Control[1]), .out(delay_2_out));
  CounterPreset #(.Bits(16)) counterpreset_1 (
    .en(or_1_out), .C(delay_1_out), .dir(delay_2_out), .in(XFER), .ld(Control[3]), .clr(Control[0]), .out(I));  // open: ovf

  // Notes on the sheet:
  //   ADDR: Addr Bus
  //   Control: 0: Clear
  //   1: Dec
  //   2: Inc
  //   3: Load
  //   4: Assert Addr
  //   5: Assert Bus
  //   XFER: default 1234
endmodule
