// Digital circuit GPR.dig as structural Verilog
module GPR (
  input  [3:0] Control,
  input  Clock,
  output [7:0] MAIN,
  output [7:0] LHS,
  output [7:0] RHS,
  output [7:0] I
);

  Register #(.Bits(8)) register_1 (.D(MAIN), .C(~Clock), .en(Control[0]), .Q(I));
  assign RHS = Control[3] ? I : 8'bz;  // Driver driver_1
  assign LHS = Control[2] ? I : 8'bz;  // Driver driver_2
  assign MAIN = Control[1] ? I : 8'bz;  // Driver driver_3

  // Notes on the sheet:
  //   Control: 0: Load
  //   1: Assert Main
  //   2: Assert LHS
  //   3: Assert RHS, default 7
endmodule
