// Digital circuit Memory.dig as structural Verilog
module Memory (
  input  [15:0] ADDR,
  input  DIR,
  input  LOAD,
  output [7:0] DATA
);

  RAMSinglePortSel #(.AddrBits(15), .Bits(8)) RAM (.A(ADDR[14:0]), .CS(ADDR[15]), .WE(~LOAD), .OE(~DIR), .D(DATA));
  EEPROM #(.AddrBits(15), .isProgramMemory("true"), .Bits(8)) ROM (
    .A(ADDR[14:0]), .CS(~ADDR[15]), .WE(~1'b1), .OE(~DIR), .D(DATA));

  // Notes on the sheet:
  //   contents of ROM (hex, n*v repeats v):
  //   1,2,3,4,5,6,7
  //   contents of ROM (hex, n*v repeats v):
  //   1,2,3,4,5,6,7
endmodule
